# Fritzing sketch Diagram (saved by Fritzing 1.0.6)
breadboards: 1

parts:
  A1 = Arduino GIGA R1 WiFi
  SM1 = 28BYJ-48 Stepper Motor [part_number=28BYJ-48]
  SM2 = 28BYJ-48 Stepper Motor [part_number=28BYJ-48]
  SM3 = 28BYJ-48 Stepper Motor [part_number=28BYJ-48]
  SM4 = 28BYJ-48 Stepper Motor [part_number=28BYJ-48]
  Driver1 = 28BYJ-48 Driver Module [part_number=ULN2003 package=THT]
  Driver2 = 28BYJ-48 Driver Module [part_number=ULN2003 package=THT]
  Driver3 = 28BYJ-48 Driver Module [part_number=ULN2003 package=THT]
  Driver4 = 28BYJ-48 Driver Module [part_number=ULN2003 package=THT]
  LCD1 = LCD screen
  Part1 = Thumb Joystick
  R1 = Rotary Potentiometer (Small) [maximum_resistance=10kΩ knob_status=50% power=0.5W package=THT]

nets:
  VDD: A1.Pin_28, A1.Pin_105, A1.Pin_123, Driver1.Vmotor, Driver2.Vmotor, Driver3.Vmotor, Driver4.Vmotor, LCD1.VDD, LCD1.LED+, Part1.VCC, R1.leg2
  GND: A1.Pin_29, A1.Pin_88, A1.Pin_106, A1.Pin_146, Driver1.GND, Driver2.GND, Driver3.GND, Driver4.GND, LCD1.VSS, LCD1.R/W, LCD1.LED-, Part1.GND, R1.leg1
  N1: A1.Pin_32, Part1.HORZ
  N2: A1.Pin_33, Part1.VERT
  N3: A1.Pin_97, Driver4.IN3
  N4: A1.Pin_98, Driver4.IN1
  N5: A1.Pin_99, Driver3.IN3
  N6: A1.Pin_100, Driver3.IN1
  N7: A1.Pin_101, Driver2.IN3
  N8: A1.Pin_102, Driver2.IN1
  N9: A1.Pin_103, Driver1.IN3
  N10: A1.Pin_104, Driver1.IN1
  N11: A1.Pin_115, Driver4.IN4
  N12: A1.Pin_116, Driver4.IN2
  N13: A1.Pin_117, Driver3.IN4
  N14: A1.Pin_118, Driver3.IN2
  N15: A1.Pin_119, Driver2.IN4
  N16: A1.Pin_120, Driver2.IN2
  N17: A1.Pin_121, Driver1.IN4
  N18: A1.Pin_122, Driver1.IN2
  N19: A1.Pin_133, LCD1.RS
  N20: A1.Pin_134, LCD1.E
  N21: A1.Pin_135, LCD1.DB4
  N22: A1.Pin_136, LCD1.DB5
  N23: A1.Pin_137, LCD1.DB6
  N24: A1.Pin_138, LCD1.DB7
  N25: A1.Pin_139, Part1.SEL
  N26: SM1.blue-pin, Driver1.blue-pin
  N27: SM1.pink-pin, Driver1.pink-pin
  N28: SM1.yellow-pin, Driver1.yellow-pin
  N29: SM1.orange-pin, Driver1.orange-pin
  N30: SM1.red-pin, Driver1.red-pin
  N31: SM2.blue-pin, Driver2.blue-pin
  N32: SM2.pink-pin, Driver2.pink-pin
  N33: SM2.yellow-pin, Driver2.yellow-pin
  N34: SM2.orange-pin, Driver2.orange-pin
  N35: SM2.red-pin, Driver2.red-pin
  N36: SM3.blue-pin, Driver3.blue-pin
  N37: SM3.pink-pin, Driver3.pink-pin
  N38: SM3.yellow-pin, Driver3.yellow-pin
  N39: SM3.orange-pin, Driver3.orange-pin
  N40: SM3.red-pin, Driver3.red-pin
  N41: SM4.blue-pin, Driver4.blue-pin
  N42: SM4.pink-pin, Driver4.pink-pin
  N43: SM4.yellow-pin, Driver4.yellow-pin
  N44: SM4.orange-pin, Driver4.orange-pin
  N45: SM4.red-pin, Driver4.red-pin
  N46: LCD1.V0, R1.wiper

custom parts:
  Arduino GIGA R1 WiFi: The Arduino GIGA R1 WiFi is designed for ambitious makers who want to step up their game.
  28BYJ-48 Stepper Motor: Unipolar Stepper Motor 28BYJ-48 Top coil - pink & orange Bottom coil - blue & yellow Common rail - red Connector pins: blue - pink - yellow - orange - red
  28BYJ-48 Driver Module: ULN2003 Driver Module for the 28BYJ-48 Unipolar Stepper Motor LED A - Blue wire - Bottom coil left LED B - Pink wire - Top coil left LED C - Yellow wire - Bottom coil right LED D - Orange wire - Top coil right Common rail - red Connector pins: blue - pink - yellow - orange - red Control pins - IN1 to IN4 Power pins - GND & Vmotor (5-12V) On/Off jumper (if removed, power to motor is cut).
